# Fritzing sketch schematic (saved by Fritzing 0.9.3b)

parts:
  M1 = DOIT Esp32 DevKit v1 (30 pins long, 11 pins width) [part_number=ESP32S-PIN30]
  M2 = MAX7219 8x8 single Led Matrix Module

nets:
  N1: M1.GND, M2.I-GND-1
  N2: M1.D18, M2.I-CLK-1
  N3: M1.D21, M2.I-CS-1
  N4: M1.D23, M2.I-DIN-1
  N5: M1.VIN, M2.I-VCC-1

notes:
  VCC -> VIN
  GND -> GND
  D IN -> 23
  CS -> 21
  SCK -> 18

custom parts:
  DOIT Esp32 DevKit v1 (30 pins long, 11 pins width): The DOIT Esp32 DevKit v1 is one of the development board created by DOIT to evaluate the ESP-WROOM-32 module. It is based on the ESP32 microcontroller that boasts Wifi, Bluetooth, Ethernet and Low Power support all in a single chip. (vanepp) made breadboard work, adjusted pin numbering and labels and reduced size of schematic and cleaned up pcb. This chip is 30pins long (2 x15) and 11 pins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
  MAX7219 8x8 single Led Matrix Module: Description: MAX7219 8x8 LedMatrix single Red Module Dimensions: 32x32mm Documents:
